// Logisim project CSE Project.circ as structural Verilog: 7 circuits, main circuit main
module main (
  input  Write_E,
  input  [3:0] in_2,
  input  [3:0] in_3,
  input  [3:0] Read_R,
  input  [15:0] in_5,
  input  Clock,
  input  Reset,
  output [15:0] Read_data_1,
  output [15:0] Read_data_2
);

  wire demultiplexer_1_out0, demultiplexer_1_out1, demultiplexer_1_out2, demultiplexer_1_out3,
       demultiplexer_1_out4, demultiplexer_1_out5, demultiplexer_1_out6, demultiplexer_1_out7,
       demultiplexer_1_out8, demultiplexer_1_out9, demultiplexer_1_out10, demultiplexer_1_out11,
       demultiplexer_1_out12, demultiplexer_1_out13, demultiplexer_1_out14, demultiplexer_1_out15;
  wire [15:0] register_1_q, register_2_q, register_3_q, register_4_q, register_5_q, register_6_q,
       register_7_q, register_8_q, register_9_q, register_10_q, register_11_q, register_12_q, register_13_q,
       register_14_q, register_15_q;

  Demultiplexer #(.select(4)) demultiplexer_1 (
    .out0(demultiplexer_1_out0), .out1(demultiplexer_1_out1), .out2(demultiplexer_1_out2),
    .out3(demultiplexer_1_out3), .out4(demultiplexer_1_out4), .out5(demultiplexer_1_out5),
    .out6(demultiplexer_1_out6), .out7(demultiplexer_1_out7), .out8(demultiplexer_1_out8),
    .out9(demultiplexer_1_out9), .out10(demultiplexer_1_out10), .out11(demultiplexer_1_out11),
    .out12(demultiplexer_1_out12), .out13(demultiplexer_1_out13), .out14(demultiplexer_1_out14),
    .out15(demultiplexer_1_out15), .in(Write_E), .sel(in_2));  // open: en
  Register #(.width(16)) register_1 (.D(in_5), .en(demultiplexer_1_out0), .Q(register_1_q), .clk(Clock), .clr(Reset));
  Register #(.width(16)) register_2 (.D(in_5), .en(demultiplexer_1_out1), .Q(register_2_q), .clk(Clock), .clr(Reset));
  Register #(.width(16)) register_3 (.D(in_5), .en(demultiplexer_1_out2), .Q(register_3_q), .clk(Clock), .clr(Reset));
  Register #(.width(16)) register_4 (.D(in_5), .en(demultiplexer_1_out3), .Q(register_4_q), .clk(Clock), .clr(Reset));
  Register #(.width(16)) register_5 (.D(in_5), .en(demultiplexer_1_out4), .Q(register_5_q), .clk(Clock), .clr(Reset));
  Register #(.width(16)) register_6 (.D(in_5), .en(demultiplexer_1_out5), .Q(register_6_q), .clk(Clock), .clr(Reset));
  Register #(.width(16)) register_7 (.D(in_5), .en(demultiplexer_1_out6), .Q(register_7_q), .clk(Clock), .clr(Reset));
  Register #(.width(16)) register_8 (.D(in_5), .en(demultiplexer_1_out7), .Q(register_8_q), .clk(Clock), .clr(Reset));
  Register #(.width(16)) register_9 (.D(in_5), .en(demultiplexer_1_out8), .Q(register_9_q), .clk(Clock), .clr(Reset));
  Register #(.width(16)) register_10 (.D(in_5), .en(demultiplexer_1_out9), .Q(register_10_q), .clk(Clock), .clr(Reset));
  Register #(.width(16)) register_11 (
    .D(in_5), .en(demultiplexer_1_out10), .Q(register_11_q), .clk(Clock), .clr(Reset));
  Register #(.width(16)) register_12 (
    .D(in_5), .en(demultiplexer_1_out11), .Q(register_12_q), .clk(Clock), .clr(Reset));
  Register #(.width(16)) register_13 (
    .D(in_5), .en(demultiplexer_1_out12), .Q(register_13_q), .clk(Clock), .clr(Reset));
  Register #(.width(16)) register_14 (
    .D(in_5), .en(demultiplexer_1_out13), .Q(register_14_q), .clk(Clock), .clr(Reset));
  Register #(.width(16)) register_15 (
    .D(in_5), .en(demultiplexer_1_out14), .Q(register_15_q), .clk(Clock), .clr(Reset));
  Register #(.width(16)) register_16 (
    .D(in_5), .en(demultiplexer_1_out15), .Q(register_15_q), .clk(Clock), .clr(Reset));
  Multiplexer #(.select(4), .width(16)) multiplexer_1 (
    .in0(register_1_q), .in1(register_2_q), .in2(register_3_q), .in3(register_4_q), .in4(register_5_q),
    .in5(register_6_q), .in6(register_7_q), .in7(register_8_q), .in8(register_9_q), .in9(register_10_q),
    .in10(register_11_q), .in11(register_12_q), .in12(register_13_q), .in13(register_14_q),
    .in14(register_15_q), .in15(register_15_q), .out(Read_data_1), .sel(in_3));  // open: en
  Multiplexer #(.select(4), .width(16)) multiplexer_2 (
    .in0(register_1_q), .in1(register_2_q), .in2(register_3_q), .in3(register_4_q), .in4(register_5_q),
    .in5(register_6_q), .in6(register_7_q), .in7(register_8_q), .in8(register_9_q), .in9(register_10_q),
    .in10(register_11_q), .in11(register_12_q), .in12(register_13_q), .in13(register_14_q),
    .in14(register_15_q), .in15(register_15_q), .out(Read_data_2), .sel(Read_R));  // open: en

  // Notes on the sheet:
  //   Rd
  //   Write data
  //    2
  //   Read R 1
endmodule

module _1_bit_ALU (
  input  Cin,
  input  A,
  input  B,
  input  [1:0] ALU_op,
  input  B_comp,
  output Result,
  output Cout
);

  wire adder_1_out, and_1_out, multiplexer_1_out, not_1_out, or_1_out, xor_1_out;

  not not_1 (not_1_out, B);
  Multiplexer multiplexer_1 (.in0(B), .in1(not_1_out), .out(multiplexer_1_out), .sel(B_comp));  // open: en
  and and_1 (and_1_out, A, B);
  or or_1 (or_1_out, A, B);
  Adder #(.width(1)) adder_1 (.a(A), .b(multiplexer_1_out), .out(adder_1_out), .cin(Cin), .cout(Cout));
  xor xor_1 (xor_1_out, A, B);
  Multiplexer #(.select(2)) multiplexer_2 (
    .in0(and_1_out), .in1(or_1_out), .in2(adder_1_out), .in3(xor_1_out), .out(Result), .sel(ALU_op));  // open: en
endmodule

module _16_bit_ALU (
  input  [1:0] ALU_OP,
  input  BCom,
  input  Cin,
  input  [15:0] in_4,
  input  [15:0] in_5,
  output [15:0] ALU_output,
  output out_7,
  output Overflow
);

  wire n1_bit_alu_1_cout, n1_bit_alu_2_cout, n1_bit_alu_3_cout, n1_bit_alu_4_cout, n1_bit_alu_5_cout,
       n1_bit_alu_6_cout, n1_bit_alu_7_cout, n1_bit_alu_8_cout, n1_bit_alu_9_cout, n1_bit_alu_10_cout,
       n1_bit_alu_11_cout, n1_bit_alu_12_cout, n1_bit_alu_13_cout, n1_bit_alu_14_cout, n1_bit_alu_15_cout,
       n1_bit_alu_16_cout;

  _1_bit_ALU u_1_bit_alu_1 (
    .A(in_5[0]), .B(in_4[0]), .Result(ALU_output[0]), .Cin(Cin), .B_comp(BCom), .Cout(n1_bit_alu_1_cout),
    .ALU_op(ALU_OP));
  _1_bit_ALU u_1_bit_alu_2 (
    .A(in_5[1]), .B(in_4[1]), .Result(ALU_output[1]), .Cin(n1_bit_alu_1_cout), .B_comp(BCom),
    .Cout(n1_bit_alu_2_cout), .ALU_op(ALU_OP));
  _1_bit_ALU u_1_bit_alu_3 (
    .A(in_5[2]), .B(in_4[2]), .Result(ALU_output[2]), .Cin(n1_bit_alu_2_cout), .B_comp(BCom),
    .Cout(n1_bit_alu_3_cout), .ALU_op(ALU_OP));
  _1_bit_ALU u_1_bit_alu_4 (
    .A(in_5[3]), .B(in_4[3]), .Result(ALU_output[3]), .Cin(n1_bit_alu_3_cout), .B_comp(BCom),
    .Cout(n1_bit_alu_4_cout), .ALU_op(ALU_OP));
  _1_bit_ALU u_1_bit_alu_5 (
    .A(in_5[4]), .B(in_4[4]), .Result(ALU_output[4]), .Cin(n1_bit_alu_4_cout), .B_comp(BCom),
    .Cout(n1_bit_alu_5_cout), .ALU_op(ALU_OP));
  _1_bit_ALU u_1_bit_alu_6 (
    .A(in_5[5]), .B(in_4[5]), .Result(ALU_output[5]), .Cin(n1_bit_alu_5_cout), .B_comp(BCom),
    .Cout(n1_bit_alu_6_cout), .ALU_op(ALU_OP));
  _1_bit_ALU u_1_bit_alu_7 (
    .A(in_5[6]), .B(in_4[6]), .Result(ALU_output[6]), .Cin(n1_bit_alu_6_cout), .B_comp(BCom),
    .Cout(n1_bit_alu_7_cout), .ALU_op(ALU_OP));
  _1_bit_ALU u_1_bit_alu_8 (
    .A(in_5[7]), .B(in_4[7]), .Result(ALU_output[7]), .Cin(n1_bit_alu_7_cout), .B_comp(BCom),
    .Cout(n1_bit_alu_8_cout), .ALU_op(ALU_OP));
  _1_bit_ALU u_1_bit_alu_9 (
    .A(in_5[8]), .B(in_4[8]), .Result(ALU_output[8]), .Cin(n1_bit_alu_8_cout), .B_comp(BCom),
    .Cout(n1_bit_alu_9_cout), .ALU_op(ALU_OP));
  _1_bit_ALU u_1_bit_alu_10 (
    .A(in_5[9]), .B(in_4[9]), .Result(ALU_output[9]), .Cin(n1_bit_alu_9_cout), .B_comp(BCom),
    .Cout(n1_bit_alu_10_cout), .ALU_op(ALU_OP));
  _1_bit_ALU u_1_bit_alu_11 (
    .A(in_5[10]), .B(in_4[10]), .Result(ALU_output[10]), .Cin(n1_bit_alu_10_cout), .B_comp(BCom),
    .Cout(n1_bit_alu_11_cout), .ALU_op(ALU_OP));
  _1_bit_ALU u_1_bit_alu_12 (
    .A(in_5[11]), .B(in_4[11]), .Result(ALU_output[11]), .Cin(n1_bit_alu_11_cout), .B_comp(BCom),
    .Cout(n1_bit_alu_12_cout), .ALU_op(ALU_OP));
  _1_bit_ALU u_1_bit_alu_13 (
    .A(in_5[12]), .B(in_4[12]), .Result(ALU_output[12]), .Cin(n1_bit_alu_12_cout), .B_comp(BCom),
    .Cout(n1_bit_alu_13_cout), .ALU_op(ALU_OP));
  _1_bit_ALU u_1_bit_alu_14 (
    .A(in_5[13]), .B(in_4[13]), .Result(ALU_output[13]), .Cin(n1_bit_alu_13_cout), .B_comp(BCom),
    .Cout(n1_bit_alu_14_cout), .ALU_op(ALU_OP));
  _1_bit_ALU u_1_bit_alu_15 (
    .A(in_5[14]), .B(in_4[14]), .Result(ALU_output[14]), .Cin(n1_bit_alu_14_cout), .B_comp(BCom),
    .Cout(n1_bit_alu_15_cout), .ALU_op(ALU_OP));
  _1_bit_ALU u_1_bit_alu_16 (
    .A(in_5[15]), .B(in_4[15]), .Result(ALU_output[15]), .Cin(n1_bit_alu_15_cout), .B_comp(BCom),
    .Cout(n1_bit_alu_16_cout), .ALU_op(ALU_OP));
  xor xor_1 (Overflow, n1_bit_alu_15_cout, n1_bit_alu_16_cout);
  nor nor_1 (out_7, ALU_output[0], ALU_output[1], ALU_output[2], ALU_output[3], ALU_output[4], ALU_output[5], ALU_output[6], ALU_output[7], ALU_output[8], ALU_output[9], ALU_output[10], ALU_output[11], ALU_output[12], ALU_output[13], ALU_output[14], ALU_output[15]);

  // Notes on the sheet:
  //   B
  //   A
  //   /Result
endmodule

module Full_data_path (
  input  BCom,
  input  Cin,
  input  Reset,
  output [3:0] Opcode,
  output [3:0] RS,
  output [3:0] RT,
  output [3:0] RD,
  output [15:0] out_8,
  output Zero,
  output [15:0] Output,
  output Overflow,
  output R_A,
  output SW,
  output LW
);

  wire ALU_srcB, clock_1_out, or_1_out, RD_RT, RegWriteE;
  wire [1:0] ALU_OP;
  wire [3:0] multiplexer_1_out;
  wire [15:0] adder_1_out, bit_extender_1_out, main_1_read_data_1, main_1_read_data_2, multiplexer_2_out,
       multiplexer_3_out, register_1_q;

  Register #(.width(16)) register_1 (.D(adder_1_out), .Q(register_1_q), .clk(clock_1_out));  // open: en, clr
  Adder #(.width(16)) adder_1 (.a(register_1_q), .b({16{1'b0}}), .out(adder_1_out));  // open: cin, cout
  ROM #(.addrWidth(16), .dataWidth(16)) rom_1 (.addr(register_1_q), .data({Opcode, RS, RT, RD}));  // open: sel
  Clock clock_1 (.out(clock_1_out));
  control_unit control_unit_1 (
    .RD(RD_RT), .RegWriteE(RegWriteE), .ALU_srcB(ALU_srcB), .C_in(Cin), .B_invert(BCom), .lw(SW), .sw(LW),
    .RESULT_ALU_RAM(R_A), .in_1(Opcode), .ALU_OP(ALU_OP));
  Multiplexer #(.width(4)) multiplexer_1 (.in0(RD), .in1(RT), .out(multiplexer_1_out), .sel(RD_RT), .en(RegWriteE));
  main main_1 (
    .Write_E(RegWriteE), .in_2(multiplexer_1_out), .in_5(multiplexer_3_out), .Clock(clock_1_out),
    .Reset(Reset), .Read_data_1(main_1_read_data_1), .in_3(RS), .Read_data_2(main_1_read_data_2), .Read_R(RT));
  assign bit_extender_1_out = {{12{1'b0}}, RD};  // Bit_Extender bit_extender_1
  Multiplexer #(.width(16)) multiplexer_2 (
    .in0(main_1_read_data_2), .in1(bit_extender_1_out), .out(multiplexer_2_out), .sel(ALU_srcB));  // open: en
  _16_bit_ALU u_16_bit_alu_1 (
    .in_4(multiplexer_2_out), .in_5(main_1_read_data_1), .ALU_output(out_8), .out_7(Zero),
    .Overflow(Overflow), .ALU_OP(ALU_OP), .BCom(BCom), .Cin(Cin));
  or or_1 (or_1_out, SW, LW);
  RAM #(.addrWidth(16), .dataWidth(16), .bus("separate")) ram_1 (
    .addr(out_8), .din(main_1_read_data_2), .data(Output), .str(SW), .sel(or_1_out), .clk(clock_1_out),
    .ld(LW));  // open: clr
  Multiplexer #(.width(16)) multiplexer_3 (.in0(Output), .in1(out_8), .out(multiplexer_3_out), .sel(R_A));  // open: en

  // Notes on the sheet:
  //   Rom
  //   contents of rom_1 (hex, n*v repeats v):
  //   123
  //   E
  //   Clock
  //   Ram
endmodule

module control_unit (
  input  [3:0] in_1,
  output RD,
  output RegWriteE,
  output ALU_srcB,
  output [1:0] ALU_OP,
  output C_in,
  output B_invert,
  output lw,
  output sw,
  output RESULT_ALU_RAM
);

  wire and_1_out, and_2_out, and_3_out, and_4_out, and_5_out, and_6_out, and_7_out, and_8_out, and_9_out,
       and_10_out, and_11_out, and_12_out, and_13_out, and_14_out, and_15_out, and_16_out, and_17_out,
       and_18_out, and_19_out, and_22_out, and_23_out, and_24_out, not_1_out, not_2_out, not_3_out,
       not_4_out, not_5_out, not_6_out, not_7_out, not_8_out, not_9_out, not_10_out, not_11_out, not_12_out,
       not_13_out, not_14_out, not_15_out, not_16_out, not_17_out, not_18_out, not_19_out, not_20_out,
       not_21_out, not_22_out, not_23_out, not_24_out, not_25_out, not_26_out, not_27_out, not_28_out,
       not_29_out, not_30_out, not_31_out, not_32_out, not_33_out, not_34_out, not_35_out, not_36_out,
       not_37_out, not_38_out, not_39_out;

  not not_1 (not_1_out, in_1[0]);
  not not_2 (not_2_out, in_1[1]);
  not not_3 (not_3_out, in_1[2]);
  not not_4 (not_4_out, in_1[1]);
  not not_5 (not_5_out, in_1[0]);
  not not_6 (not_6_out, in_1[2]);
  not not_7 (not_7_out, in_1[0]);
  not not_8 (not_8_out, in_1[3]);
  not not_9 (not_9_out, in_1[0]);
  not not_10 (not_10_out, in_1[1]);
  not not_11 (not_11_out, in_1[0]);
  not not_12 (not_12_out, in_1[1]);
  not not_13 (not_13_out, in_1[2]);
  not not_14 (not_14_out, in_1[1]);
  not not_15 (not_15_out, in_1[0]);
  not not_16 (not_16_out, in_1[1]);
  not not_17 (not_17_out, in_1[0]);
  not not_18 (not_18_out, in_1[0]);
  not not_19 (not_19_out, in_1[2]);
  not not_20 (not_20_out, in_1[1]);
  not not_21 (not_21_out, in_1[3]);
  not not_22 (not_22_out, in_1[1]);
  not not_23 (not_23_out, in_1[0]);
  not not_24 (not_24_out, in_1[1]);
  not not_25 (not_25_out, in_1[2]);
  not not_26 (not_26_out, in_1[0]);
  not not_27 (not_27_out, in_1[0]);
  not not_28 (not_28_out, in_1[1]);
  not not_29 (not_29_out, in_1[2]);
  not not_30 (not_30_out, in_1[0]);
  not not_31 (not_31_out, in_1[0]);
  not not_32 (not_32_out, in_1[1]);
  not not_33 (not_33_out, in_1[3]);
  not not_34 (not_34_out, in_1[0]);
  not not_35 (not_35_out, in_1[1]);
  not not_36 (not_36_out, in_1[0]);
  not not_37 (not_37_out, in_1[2]);
  not not_38 (not_38_out, in_1[0]);
  not not_39 (not_39_out, in_1[1]);
  and and_1 (and_1_out, not_1_out, in_1[2]);
  and and_2 (and_2_out, in_1[0], not_2_out, not_3_out);
  or or_1 (RD, and_1_out, and_2_out, and_3_out);
  and and_3 (and_3_out, in_1[0], not_4_out, in_1[3]);
  and and_4 (and_4_out, not_5_out, not_6_out);
  and and_5 (and_5_out, not_7_out, not_8_out);
  and and_6 (and_6_out, not_9_out, in_1[1]);
  and and_7 (and_7_out, in_1[0], not_10_out);
  and and_8 (and_8_out, not_11_out, in_1[2]);
  or or_2 (ALU_srcB, and_8_out, and_9_out, and_10_out);
  and and_9 (and_9_out, in_1[0], not_12_out, not_13_out);
  and and_10 (and_10_out, in_1[0], not_14_out, in_1[3]);
  and and_11 (and_11_out, not_15_out, not_16_out);
  or or_3 (ALU_OP[1], and_11_out, and_12_out);
  and and_12 (and_12_out, not_17_out, in_1[2]);
  and and_13 (and_13_out, not_18_out, in_1[1], not_19_out, in_1[3]);
  and and_14 (and_14_out, in_1[0], not_20_out, not_21_out);
  and and_15 (and_15_out, in_1[0], not_22_out, in_1[2]);
  and and_16 (and_16_out, not_23_out, not_24_out, not_25_out, in_1[3]);
  and and_17 (and_17_out, not_26_out, in_1[1], in_1[2], in_1[3]);
  and and_18 (and_18_out, not_27_out, not_28_out, not_29_out, in_1[3]);
  and and_19 (and_19_out, not_30_out, in_1[1], in_1[2], in_1[3]);
  and and_20 (lw, not_31_out, not_32_out, in_1[2], not_33_out);
  and and_21 (sw, not_34_out, not_35_out, in_1[2], in_1[3]);
  and and_22 (and_22_out, not_36_out, not_37_out);
  and and_23 (and_23_out, not_38_out, in_1[1]);
  or or_4 (RESULT_ALU_RAM, and_22_out, and_23_out, and_24_out);
  and and_24 (and_24_out, in_1[0], not_39_out);
  or or_5 (RegWriteE, and_4_out, and_5_out, and_6_out, and_7_out);
  or or_6 (ALU_OP[0], and_13_out, and_14_out, and_15_out);
  or or_7 (C_in, and_16_out, and_17_out);
  or or_8 (B_invert, and_18_out, and_19_out);
endmodule

module _16_ALU (
  input  Cin,
  input  [15:0] A,
  input  [15:0] B,
  input  [1:0] ALU_op,
  input  B_invert,
  output [15:0] Result
);

  wire [15:0] adder_1_out, and_1_out, multiplexer_1_out, not_1_out, or_1_out, xor_1_out;

  assign not_1_out = ~B;  // NOT_Gate not_1, 16 bits wide
  Multiplexer #(.width(16)) multiplexer_1 (
    .in0(B), .in1(not_1_out), .out(multiplexer_1_out), .sel(B_invert));  // open: en
  assign and_1_out = A & B;  // AND_Gate and_1, 16 bits wide
  assign or_1_out = A | B;  // OR_Gate or_1, 16 bits wide
  Adder #(.width(16)) adder_1 (.a(A), .b(multiplexer_1_out), .out(adder_1_out), .cin(Cin));  // open: cout
  assign xor_1_out = A ^ B;  // XOR_Gate xor_1, 16 bits wide
  Multiplexer #(.select(2), .width(16)) multiplexer_2 (
    .in0(and_1_out), .in1(or_1_out), .in2(adder_1_out), .in3(xor_1_out), .out(Result), .sel(ALU_op));  // open: en
endmodule

module R_Type (
  input  BCom,
  input  Cin,
  input  [1:0] ALU_OP,
  input  Clock,
  input  Reset,
  output [3:0] Opcode,
  output [3:0] RS,
  output [3:0] RT,
  output [3:0] RD,
  output [15:0] out_10,
  output Zero,
  output Overflow,
  output [15:0] out_13
);

  wire clock_1_out;
  wire [15:0] n16_bit_alu_1_alu_output, register_1_q;

  Register #(.width(16)) register_1 (.Q(register_1_q));  // open: D, en, clk, clr
  ROM #(.addrWidth(16), .dataWidth(16)) rom_1 (.addr(register_1_q), .data({Opcode, RS, RT, RD}));  // open: sel
  main main_1 (
    .Write_E(Clock), .in_2(RD), .in_5(n16_bit_alu_1_alu_output), .Clock(clock_1_out), .Reset(Reset),
    .Read_data_1(out_10), .in_3(RS), .Read_data_2(out_13), .Read_R(RT));
  Clock clock_1 (.out(clock_1_out));
  _16_bit_ALU u_16_bit_alu_1 (
    .in_4(out_13), .in_5(out_10), .ALU_output(n16_bit_alu_1_alu_output), .out_7(Zero), .Overflow(Overflow),
    .ALU_OP(ALU_OP), .BCom(BCom), .Cin(Cin));

  // Notes on the sheet:
  //   contents of rom_1 (hex, n*v repeats v):
  //   48a4
  //   E
  //   Read R1
  //   Read R2
endmodule
